# Fritzing sketch Radio Lolin32+PCM5102+PAM8403 (saved by Fritzing 0.9.9b)
breadboards: 1

parts:
  MCU1 = Wemos Lolin32lite
  LCD1 = TFT 1.8 inch 160x128 w microSD
  SPKR1 = Loudspeaker
  SPKR2 = Loudspeaker
  Componente1 = Adafruit UDA1334 I2S DAC [part_number="Adafruit #3678"]
  M1 = PAM8403 Stereo Amplifier with Volume Control [part_number=HW-012]
  S1 = Pushbutton [package="[THT]"]
  S2 = Pushbutton [package="[THT]"]

nets:
  N1: MCU1.pin_8, Componente1.DATA_IN
  N2: MCU1.pin_9, Componente1.BITCLK_IN
  N3: MCU1.pin_10, Componente1.WORDSEL_IN
  N4: MCU1.pin_13, LCD1.pin_1, Componente1.GND, M1.POWER-, S1.Pin_1, S1.Pin_2, S2.Pin_1, S2.Pin_2
  N5: MCU1.pin_18, LCD1.pin_6
  N6: MCU1.pin_21, S1.Pin_3, S1.Pin_4
  N7: MCU1.pin_22, S2.Pin_3, S2.Pin_4
  N8: MCU1.pin_23, LCD1.pin_10
  N9: MCU1.pin_24, LCD1.pin_7
  N10: MCU1.pin_25, LCD1.pin_8
  N11: MCU1.pin_27, LCD1.pin_9
  N12: MCU1.pin_28, LCD1.pin2, LCD1.pin_15, Componente1.VIN, M1.POWER+
  N13: SPKR1.pin1, M1.LOUT-
  N14: SPKR1.pin2, M1.LOUT+
  N15: SPKR2.pin1, M1.ROUT-
  N16: SPKR2.pin2, M1.ROUT+
  N17: Componente1.OUTL, M1.INPUTL
  N18: Componente1.AGND, M1.INPUTG
  N19: Componente1.OUTR, M1.INPUTR

notes:
  CS SCL MOSI DC RST
  A0
  RESET      2 (18)
  DC           18 (24)
  MOSI       23 (25)
  SCL          22 (27)
  CS            5 (23)
  PCM5102A

custom parts:
  Wemos Lolin32lite: Wemos Lolinlite32 wifi and blue tooth board based on the ESP-32 cpu, digital I/Os 19, analog inputs 6, clock 240mhz, Flash 4Mbytes, lipo battery charger (500ma connection broken out on breadboard but not pcb), usb.
  TFT 1.8 inch 160x128 w microSD: This is the kmr-1.8 spi lcd display available on ebay and others. The 1.8" display has 128x160 color pixels.
  Adafruit UDA1334 I2S DAC: This fully-featured UDA1334A I2S Stereo DAC breakout is a perfect match for any I2S-output audio interface. It's affordable but sounds great! The NXP UDA1334A is a jack-of-all-I2S-trades: you can use 3.3V - 5V logic levels (a rarity), and can process multiple different formats by setting two pins to high or low. The DAC will process data immediately, and give you a clear, analog, stereo line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
  PAM8403 Stereo Amplifier with Volume Control: PAM8403 stereo amplifier module with volume control Descriptive words Links: PAM8403 product datasheet
